# Fritzing sketch ESP8266-DHT11-LCD1602_I2C-SG90-2RC522 (saved by Fritzing 0.9.3b)
breadboards: 1

parts:
  元件1 = LCD1602-I2C
  SERVO1 = Tower Pro SG90 servo [part_number=101246]
  元件2 = RFID-RC522-v3
  U1 = NodeMCU V3.0
  元件3 = RFID-RC522-v3
  DHT1 = DHT11 Humitidy and Temperature Sensor (3 pins)

nets:
  GND: 元件1.GND, U1.GND#6, U1.GND#13, U1.GND#16, DHT1.GND
  VCC: 元件1.VCC, U1.Vin
  N1: 元件1.SDA, U1.D2
  N2: 元件1.SCL, U1.D1
  N3: SERVO1.Signal, U1.D0
  +5V: SERVO1.+5V, U1.3V3, 元件3.3.3V, DHT1.VDD
  GND_2: SERVO1.GND, 元件2.GND, U1.GND#41, 元件3.GND
  N4: 元件2.SDA, U1.D4
  N5: 元件2.SCK, U1.D5, 元件3.SCK
  N6: 元件2.MOSI, U1.D7, 元件3.MOSI
  N7: 元件2.MISO, U1.D6, 元件3.MISO
  N8: 元件2.RST, U1.D3, 元件3.RST
  N9: 元件2.3.3V, U1.VU
  N10: U1.D8, 元件3.SDA
  N11: U1.RX, DHT1.DATA

notes:
  Reader1
  Reader0
  RC522 Reader0 | ESP8266
  SDA | D8
  SCK | D5
  MOSI | D7
  MISO | D6
  IRQ |
  GND | GND
  RST | D3
  3.3V | 3V3
  -------------------------------------------
  RC522 Reader1 | ESP8266
  SDA | D4
  SCK | D5
  MOSI | D7
  MISO | D6
  IRQ |
  GND | GND
  RST | D3
  3.3V | VU
  -------------------------------------------
  LCD1602_I2C | ESP8266
  SCL | D1
  SDA | D2
  VCC | Vin
  GND | GND
  -------------------------------------------
  DHT11 | ESP8266
  DATA | RX
  VDD | 3V3
  GND | GND
  -------------------------------------------
  SG90 | ESP8266
  Signal | D0
  VDD | 3V3
  GND | GND
  接线颜色图例：
  SDA
  SCK
  MOSI
  MISO
  RST
  SCL
  DATA
  Signal
  +5V
  +3.3V
  GND

custom parts:
  LCD1602-I2C: A standard character display, usually with 2x16 characters. Comes in many colors with LCM1602 IIC attached.
  Tower Pro SG90 servo: Original file by John De Cristofaro http://www.adafruit.com/products/1449 Adafruit Feedback Servo (Small) Edited by: e-radionica.com 28/9/2015
  RFID-RC522-v3: A simple China made RFID-RC522 Reader (6x4 cm); do check the pin labels, as this is a MFRC522 based clone.
  NodeMCU V3.0: ESP8266 based NodeMCU
  DHT11 Humitidy and Temperature Sensor (3 pins): DHT11 Humidity and Temperature Sensor (3 pins) from the design created by John De Cristofaro for Adafruit Industries.
