# Fritzing sketch ESP8266-DHT11-LCD1602_I2C-SG90-RC522 (saved by Fritzing 0.9.3b)
breadboards: 1

parts:
  U1 = NodeMCU V3.0
  元件1 = LCD1602-I2C
  DHT1 = DHT11 Humitidy and Temperature Sensor (3 pins)
  SERVO1 = Tower Pro SG90 servo [part_number=101246]
  元件2 = RFID-RC522-v3

nets:
  N1: U1.D0, SERVO1.Signal
  N2: U1.D1, 元件1.SCL
  N3: U1.D2, 元件1.SDA
  N4: U1.D3, 元件2.RST
  3V3: U1.3V3, DHT1.VDD, SERVO1.+5V, 元件2.3.3V
  GND: U1.GND, 元件1.GND, DHT1.GND, SERVO1.GND, 元件2.GND
  N5: U1.D5, 元件2.SCK
  N6: U1.D6, 元件2.MISO
  N7: U1.D7, 元件2.MOSI
  N8: U1.D8, 元件2.SDA
  N9: U1.RX, DHT1.DATA
  VIN: U1.Vin, 元件1.VCC

notes:
  RC522 Reader | ESP8266
  SDA | D8
  SCK | D5
  MOSI | D7
  MISO | D6
  IRQ |
  GND | GND
  RST | D3
  3.3V | 3V3
  -------------------------------------------
  LCD1602_I2C | ESP8266
  SCL | D1
  SDA | D2
  VCC | Vin
  GND | GND
  -------------------------------------------
  DHT11 | ESP8266
  DATA | RX
  VDD | 3V3
  GND | GND
  -------------------------------------------
  SG90 | ESP8266
  Signal | D0
  VDD | 3V3
  GND | GND
  接线颜色图例：
  SDA
  SCK
  MOSI
  MISO
  RST
  SCL
  DATA
  Signal
  +5V
  +3.3V
  GND

custom parts:
  NodeMCU V3.0: ESP8266 based NodeMCU
  LCD1602-I2C: A standard character display, usually with 2x16 characters. Comes in many colors with LCM1602 IIC attached.
  DHT11 Humitidy and Temperature Sensor (3 pins): DHT11 Humidity and Temperature Sensor (3 pins) from the design created by John De Cristofaro for Adafruit Industries.
  Tower Pro SG90 servo: Original file by John De Cristofaro http://www.adafruit.com/products/1449 Adafruit Feedback Servo (Small) Edited by: e-radionica.com 28/9/2015
  RFID-RC522-v3: A simple China made RFID-RC522 Reader (6x4 cm); do check the pin labels, as this is a MFRC522 based clone.
