# Fritzing sketch ESP8266-DHT11-LCD1602_I2C-SG90 (saved by Fritzing 0.9.3b)
breadboards: 1

parts:
  U1 = NodeMCU V3.0
  元件1 = LCD1602-I2C
  DHT1 = DHT11 Humitidy and Temperature Sensor (3 pins)
  SERVO1 = Tower Pro SG90 servo [part_number=101246]

nets:
  N1: U1.D1, 元件1.SCL
  N2: U1.D2, 元件1.SDA
  N3: U1.D4, SERVO1.Signal
  3V3: U1.3V3, DHT1.VDD, SERVO1.+5V
  GND: U1.GND#6, U1.GND#13, U1.GND#16, U1.GND#33, 元件1.GND, SERVO1.GND
  N4: U1.RX, DHT1.DATA
  VIN: U1.Vin, 元件1.VCC
  N5: U1.GND#41, DHT1.GND

custom parts:
  NodeMCU V3.0: ESP8266 based NodeMCU
  LCD1602-I2C: A standard character display, usually with 2x16 characters. Comes in many colors with LCM1602 IIC attached.
  DHT11 Humitidy and Temperature Sensor (3 pins): DHT11 Humidity and Temperature Sensor (3 pins) from the design created by John De Cristofaro for Adafruit Industries.
  Tower Pro SG90 servo: Original file by John De Cristofaro http://www.adafruit.com/products/1449 Adafruit Feedback Servo (Small) Edited by: e-radionica.com 28/9/2015
